// Logisim project cpu.circ as structural Verilog: 1 circuit, main circuit main
module main (
  input  [31:0] RS_READ_VALUE,
  input  [31:0] RT_READ_VALUE,
  input  [31:0] INSTRUCTION,
  input  CLOCK,
  input  RESET,
  input  op,
  input  op_2,
  input  op_3,
  output [31:0] t0,
  output [31:0] t1,
  output [31:0] t2,
  output [31:0] t3,
  output [4:0] RS,
  output [4:0] RT,
  output [4:0] Write_Register,
  output [31:0] RD_WRITE_VALUE,
  output RD_WRITE_ENABLE,
  output [23:0] FETCH_ADDRESS,
  output MemWrite
);

  wire add, addiu, addu, \and , andi, beq, bitpal, bne, comparator_1_eq, comparator_2_eq, comparator_3_eq,
       comparator_4_eq, comparator_5_eq, comparator_6_eq, comparator_7_eq, comparator_8_eq, comparator_22_eq,
       comparator_23_eq, comparator_24_eq, comparator_25_eq, comparator_26_eq, comparator_27_eq,
       comparator_28_eq, comparator_29_eq, comparator_30_eq, comparator_31_eq, comparator_32_eq,
       comparator_33_eq, comparator_34_eq, comparator_35_eq, itype, j, jal, jr, Jtype, lb, lbu, lfsr, lui,
       lw, \or , or_1_out, or_2_out, or_5_out, ori, rs_not_t, rt_not_t, Rtype, sll, slt, sltu, sra, srl, sub,
       subu, sw, undriven, zero_ext;
  wire [1:0] bit_extender_1_out, bit_extender_2_out;
  wire [4:0] rd, shamt, subtractor_1_out, subtractor_2_out;
  wire [5:0] funct, op_t;
  wire [15:0] immediate;
  wire [25:0] addresss;
  wire [31:0] and_1_out, and_2_out, and_3_out, and_4_out, and_5_out, and_6_out, and_7_out, and_8_out,
       bit_extender_3_out, bit_extender_4_out, Data1, Data2, Data_imme, rsout0, rtout0, shifter_1_out,
       shifter_2_out, shifter_3_out, shifter_4_out, shifter_5_out, shifter_6_out, shifter_7_out,
       shifter_8_out;

  Comparator #(.width(5), .mode("unsigned")) comparator_1 (.a(RS), .b(5'b01000), .eq(comparator_1_eq));  // open: gt, lt
  Comparator #(.width(5), .mode("unsigned")) comparator_2 (.a(RS), .b(5'b01001), .eq(comparator_2_eq));  // open: gt, lt
  Comparator #(.width(5), .mode("unsigned")) comparator_3 (.a(RS), .b(5'b01010), .eq(comparator_3_eq));  // open: gt, lt
  Comparator #(.width(5), .mode("unsigned")) comparator_4 (.a(RS), .b(5'b01011), .eq(comparator_4_eq));  // open: gt, lt
  Comparator #(.width(5), .mode("unsigned")) comparator_5 (.a(RT), .b(5'b01000), .eq(comparator_5_eq));  // open: gt, lt
  Comparator #(.width(5), .mode("unsigned")) comparator_6 (.a(RT), .b(5'b01001), .eq(comparator_6_eq));  // open: gt, lt
  Comparator #(.width(5), .mode("unsigned")) comparator_7 (.a(RT), .b(5'b01010), .eq(comparator_7_eq));  // open: gt, lt
  Comparator #(.width(5), .mode("unsigned")) comparator_8 (.a(RT), .b(5'b01011), .eq(comparator_8_eq));  // open: gt, lt
  or or_1 (or_1_out, comparator_1_eq, comparator_2_eq, comparator_3_eq, comparator_4_eq);
  or or_2 (or_2_out, comparator_5_eq, comparator_6_eq, comparator_7_eq, comparator_8_eq);
  or or_3 (zero_ext, addiu, lbu);
  Comparator #(.width(6)) comparator_9 (.a(op_t), .b({6{1'b0}}), .eq(Rtype));  // open: gt, lt
  Comparator #(.width(6)) comparator_10 (.a(op_t), .b(6'b000010), .eq(j));  // open: gt, lt
  Comparator #(.width(6)) comparator_11 (.a(op_t), .b(6'b000011), .eq(jal));  // open: gt, lt
  Comparator #(.width(6)) comparator_12 (.a(op_t), .b(6'b001001), .eq(addiu));  // open: gt, lt
  Comparator #(.width(6)) comparator_13 (.a(op_t), .b(6'b001100), .eq(andi));  // open: gt, lt
  Comparator #(.width(6)) comparator_14 (.a(op_t), .b(6'b001101), .eq(ori));  // open: gt, lt
  Comparator #(.width(6)) comparator_15 (.a(op_t), .b(6'b001111), .eq(lui));  // open: gt, lt
  Comparator #(.width(6)) comparator_16 (.a(op_t), .b(6'b100000), .eq(lb));  // open: gt, lt
  Comparator #(.width(6)) comparator_17 (.a(op_t), .b(6'b100100), .eq(lbu));  // open: gt, lt
  Comparator #(.width(6)) comparator_18 (.a(op_t), .b(6'b100011), .eq(lw));  // open: gt, lt
  Comparator #(.width(6)) comparator_19 (.a(op_t), .b(6'b101011), .eq(sw));  // open: gt, lt
  Comparator #(.width(6)) comparator_20 (.a(op_t), .b(6'b000100), .eq(beq));  // open: gt, lt
  Comparator #(.width(6)) comparator_21 (.a(op_t), .b(6'b000101), .eq(bne));  // open: gt, lt
  not not_1 (rs_not_t, or_1_out);
  not not_2 (rt_not_t, or_2_out);
  or or_4 (Jtype, j, jal);
  or or_5 (or_5_out, Jtype, Rtype);
  Subtractor #(.width(5)) subtractor_1 (.a(RS), .b(5'b01000), .out(subtractor_1_out));  // open: bin, bout
  Subtractor #(.width(5)) subtractor_2 (.a(RT), .b(5'b01000), .out(subtractor_2_out));  // open: bin, bout
  not not_3 (itype, or_5_out);
  Bit_Extender #(.in_width(5), .out_width(2)) bit_extender_1 (.in(subtractor_1_out), .out(bit_extender_1_out));
  Bit_Extender #(.in_width(5), .out_width(2)) bit_extender_2 (.in(subtractor_2_out), .out(bit_extender_2_out));
  assign bit_extender_3_out = {{16{1'b0}}, immediate};  // Bit_Extender bit_extender_3
  assign bit_extender_4_out = {{16{immediate[15]}}, immediate};  // Bit_Extender bit_extender_4
  regfile_main RegFile (
    .Read_register_1(bit_extender_1_out), .Read_register_2(bit_extender_2_out), .t0_Value(t0), .t1_Value(t1),
    .t2_Value(t2), .t3_Value(t3), .clock(CLOCK), .Read_Data_1(rsout0), .Read_Data_2(rtout0));  // open: write_register, write_data, RegWrite
  Multiplexer #(.width(32)) multiplexer_1 (
    .in0(bit_extender_3_out), .in1(bit_extender_4_out), .out(Data_imme), .sel(zero_ext));  // open: en
  // mem_main MEM: pin names not known
  // alu_main ALU: pin names not known
  assign and_1_out = INSTRUCTION & 32'hfc000000;  // AND_Gate and_1, 32 bits wide
  assign and_2_out = INSTRUCTION & 32'h3e00000;  // AND_Gate and_2, 32 bits wide
  assign and_3_out = INSTRUCTION & 32'h1f0000;  // AND_Gate and_3, 32 bits wide
  assign and_4_out = INSTRUCTION & 32'hf800;  // AND_Gate and_4, 32 bits wide
  assign and_5_out = INSTRUCTION & 32'h7c00;  // AND_Gate and_5, 32 bits wide
  assign and_6_out = INSTRUCTION & 32'h3f;  // AND_Gate and_6, 32 bits wide
  assign and_7_out = INSTRUCTION & 32'hffff;  // AND_Gate and_7, 32 bits wide
  assign and_8_out = INSTRUCTION & 32'h3ffffff;  // AND_Gate and_8, 32 bits wide
  Shifter #(.width(32), .shift("lr")) shifter_1 (.in(and_1_out), .\dist (5'b11010), .out(shifter_1_out));
  Shifter #(.width(32), .shift("lr")) shifter_2 (.in(and_2_out), .\dist (5'b10101), .out(shifter_2_out));
  Shifter #(.width(32), .shift("lr")) shifter_3 (.in(and_3_out), .\dist (5'b10000), .out(shifter_3_out));
  Shifter #(.width(32), .shift("lr")) shifter_4 (.in(and_4_out), .\dist (5'b01011), .out(shifter_4_out));
  Shifter #(.width(32), .shift("lr")) shifter_5 (.in(and_5_out), .\dist (5'b00110), .out(shifter_5_out));
  Shifter #(.width(32), .shift("lr")) shifter_6 (.in(and_6_out), .\dist ({5{1'b0}}), .out(shifter_6_out));
  Shifter #(.width(32), .shift("lr")) shifter_7 (.in(and_7_out), .\dist ({5{1'b0}}), .out(shifter_7_out));
  Shifter #(.width(32), .shift("lr")) shifter_8 (.in(and_8_out), .\dist ({5{1'b0}}), .out(shifter_8_out));
  Bit_Extender #(.in_width(32), .out_width(6)) bit_extender_5 (.in(shifter_1_out), .out(op_t));
  Bit_Extender #(.in_width(32), .out_width(5)) bit_extender_6 (.in(shifter_2_out), .out(RS));
  Bit_Extender #(.in_width(32), .out_width(5)) bit_extender_7 (.in(shifter_3_out), .out(RT));
  Bit_Extender #(.in_width(32), .out_width(5)) bit_extender_8 (.in(shifter_4_out), .out(rd));
  Bit_Extender #(.in_width(32), .out_width(5)) bit_extender_9 (.in(shifter_5_out), .out(shamt));
  Bit_Extender #(.in_width(32), .out_width(6)) bit_extender_10 (.in(shifter_6_out), .out(funct));
  Bit_Extender #(.in_width(32)) bit_extender_11 (.in(shifter_7_out), .out(immediate));
  Bit_Extender #(.in_width(32), .out_width(26)) bit_extender_12 (.in(shifter_8_out), .out(addresss));
  // Probe on op_t
  // Probe on RS
  // Probe on RT
  // Probe on rd
  // Probe on shamt
  // Probe on funct
  Comparator #(.width(6)) comparator_22 (.a(funct), .b(6'b100000), .eq(comparator_22_eq));  // open: gt, lt
  Comparator #(.width(6)) comparator_23 (.a(funct), .b(6'b100001), .eq(comparator_23_eq));  // open: gt, lt
  Comparator #(.width(6)) comparator_24 (.a(funct), .b(6'b100010), .eq(comparator_24_eq));  // open: gt, lt
  Comparator #(.width(6)) comparator_25 (.a(funct), .b(6'b100011), .eq(comparator_25_eq));  // open: gt, lt
  Comparator #(.width(6)) comparator_26 (.a(funct), .b(6'b100100), .eq(comparator_26_eq));  // open: gt, lt
  Comparator #(.width(6)) comparator_27 (.a(funct), .b(6'b100101), .eq(comparator_27_eq));  // open: gt, lt
  Comparator #(.width(6)) comparator_28 (.a(funct), .b(6'b101010), .eq(comparator_28_eq));  // open: gt, lt
  Comparator #(.width(6)) comparator_29 (.a(funct), .b(6'b101011), .eq(comparator_29_eq));  // open: gt, lt
  Comparator #(.width(6)) comparator_30 (.a(funct), .b(6'b001000), .eq(comparator_30_eq));  // open: gt, lt
  Comparator #(.width(6)) comparator_31 (.a(funct), .b({6{1'b0}}), .eq(comparator_31_eq));  // open: gt, lt
  Comparator #(.width(6)) comparator_32 (.a(funct), .b(6'b000010), .eq(comparator_32_eq));  // open: gt, lt
  Comparator #(.width(6)) comparator_33 (.a(funct), .b(6'b000011), .eq(comparator_33_eq));  // open: gt, lt
  Comparator #(.width(6)) comparator_34 (.a(funct), .b(6'b111110), .eq(comparator_34_eq));  // open: gt, lt
  Comparator #(.width(6)) comparator_35 (.a(funct), .b({6{1'b1}}), .eq(comparator_35_eq));  // open: gt, lt
  // Probe on immediate
  // Probe on addresss
  and and_9 (add, comparator_22_eq, Rtype);
  and and_10 (addu, comparator_23_eq, Rtype);
  and and_11 (sub, comparator_24_eq, Rtype);
  and and_12 (subu, comparator_25_eq, Rtype);
  and and_13 (\and , comparator_26_eq, Rtype);
  and and_14 (\or , comparator_27_eq, Rtype);
  and and_15 (slt, comparator_28_eq, Rtype);
  and and_16 (sltu, comparator_29_eq, Rtype);
  and and_17 (jr, comparator_30_eq, Rtype);
  and and_18 (sll, comparator_31_eq, Rtype);
  and and_19 (srl, comparator_32_eq, Rtype);
  and and_20 (sra, comparator_33_eq, Rtype);
  and and_21 (bitpal, comparator_34_eq, Rtype);
  and and_22 (lfsr, comparator_35_eq, Rtype);
  Multiplexer #(.width(32)) multiplexer_2 (.in0(rsout0), .in1(RS_READ_VALUE), .out(Data1), .sel(rs_not_t));  // open: en
  Multiplexer #(.width(32)) multiplexer_3 (.in0(rtout0), .in1(RT_READ_VALUE), .out(Data2), .sel(rt_not_t));  // open: en
  Multiplexer multiplexer_4 (.in0(op), .in1(op_2), .out(MemWrite), .sel(op_3), .en(undriven));
  Adder #(.width(2)) adder_1 ();  // open: a, b, out, cin, cout

  // Other names for the same wires on the sheet: FETCH_ADDRES[23:0] = FETCH_ADDRESS;
  //   RD_WRITE_VALU[31:0] = RD_WRITE_VALUE; RT_READ_VALU[31:0] = RT_READ_VALUE

  // Notes on the sheet:
  //   These are outputs/inputs from run.circ
  //   Select function
  //   Data Preparation
  //   Decode
  //   TEST
endmodule
